# Fritzing sketch Esquemaa (saved by Fritzing 0.9.3b)

parts:
  Componente1 = Arduino Uno (Rev3)  # not connected
  M1 = DC Motor  # not connected
  M2 = DC Motor  # not connected
  Componente2 = AF_mshield-v11_1
  S1 = Pololu QTR-8 Reflectabce Sensor array [package=THT]

nets:
  N1: Componente2.3#89, S1.pin11
  N2: Componente2.PWM0A, S1.pin12
  N3: Componente2.1, S1.pin3, S1.pin5
  N4: Componente2.2, S1.pin4, S1.pin6
  N5: Componente2.3#111, S1.pin7
  N6: Componente2.4, S1.pin8
  N7: Componente2.5, S1.pin9
  N8: Componente2.6, S1.pin10
  N9: Componente2.VCC, S1.pin2, S1.pin14
  N10: Componente2.GND, S1.pin15
